// Logisim project VRAC.circ as structural Verilog: 8 circuits, main circuit main
module main (
  input  in_1
);

  wire [4:0] undriven, undriven_2;
  wire [31:0] register_file_1_r1d, register_file_1_r2d, undriven_3;

  // ROM #(.addrWidth(16), .line("quad")) rom_1: pin names not known; wires that end beside it: {16{1'b0}}
  register_file register_file_1 (
    .clock(in_1), .WE(1'b1), .R1(undriven), .R2(undriven_2), .WD(undriven_3), .R1D(register_file_1_r1d),
    .R2D(register_file_1_r2d));  // open: reset
  Adder #(.width(32)) adder_1 (.a(register_file_1_r1d), .b(register_file_1_r2d));  // open: out, cin, cout
  RAM #(.addrWidth(16), .asyncread("true"), .byteenables("byteEnables"), .clearpin("true"), .dataWidth(32)) ram_1 (
    .addr({16{1'b0}}), .we(1'b1), .oe(1'b1), .be3(in_1));  // open: clk, din, dout, clr, be2, be1, be0

  // Notes on the sheet:
  //   contents of rom_1 (hex, n*v repeats v):
  //   2 3
endmodule

module ALU (
  input  [4:0] select_oper,
  input  [31:0] data_0,
  input  [31:0] data_1,
  output [31:0] out_4,
  output out_5
);

  wire adder_1_cout, adder_2_cout, comparator_1_eq, comparator_2_eq, comparator_3_lt, comparator_4_lt,
       subtractor_1_bout, subtractor_2_bout, undriven, undriven_2, undriven_3, undriven_4;
  wire [31:0] adder_1_out, adder_2_out, divider_1_out, divider_1_rem, divider_2_out, divider_2_rem,
       fpadder_1_out, fpdivider_1_out, fpmultiplier_1_out, fpsubtractor_1_out, multiplier_1_cout,
       multiplier_1_out, multiplier_2_cout, multiplier_2_out, shifter_1_out, shifter_2_out, shifter_3_out,
       subtractor_1_out, subtractor_2_out;

  Comparator #(.width(32)) comparator_1 (.a({32{1'b0}}), .b(divider_2_rem), .eq(comparator_1_eq));  // open: gt, lt
  Comparator #(.width(32)) comparator_2 (.a({32{1'b0}}), .b(divider_1_rem), .eq(comparator_2_eq));  // open: gt, lt
  Comparator #(.width(32)) comparator_3 (.a({32{1'b0}}), .b(multiplier_2_cout), .lt(comparator_3_lt));  // open: gt, eq
  Comparator #(.width(32)) comparator_4 (.a({32{1'b0}}), .b(multiplier_1_cout), .lt(comparator_4_lt));  // open: gt, eq
  Adder #(.width(32)) adder_1 (.a(data_0), .b(data_1), .out(adder_1_out), .cout(adder_1_cout));  // open: cin
  Adder #(.width(32)) adder_2 (.a(data_0), .b(data_1), .out(adder_2_out), .cout(adder_2_cout));  // open: cin
  FPAdder fpadder_1 (.a(data_0), .b(data_1), .out(fpadder_1_out));
  Subtractor #(.width(32)) subtractor_1 (
    .a(data_0), .b(data_1), .out(subtractor_1_out), .bout(subtractor_1_bout));  // open: bin
  Subtractor #(.width(32)) subtractor_2 (
    .a(data_0), .b(data_1), .out(subtractor_2_out), .bout(subtractor_2_bout));  // open: bin
  FPSubtractor fpsubtractor_1 (.a(data_0), .b(data_1), .out(fpsubtractor_1_out));
  Multiplier #(.width(32)) multiplier_1 (
    .a(data_0), .b(data_1), .out(multiplier_1_out), .cout(multiplier_1_cout));  // open: cin
  Multiplier #(.width(32)) multiplier_2 (
    .a(data_0), .b(data_1), .out(multiplier_2_out), .cout(multiplier_2_cout));  // open: cin
  FPMultiplier fpmultiplier_1 (.a(data_0), .b(data_1), .out(fpmultiplier_1_out));
  Divider #(.width(32)) divider_1 (.a(data_0), .b(data_1), .out(divider_1_out), .rem(divider_1_rem));  // open: upper
  Divider #(.width(32)) divider_2 (.a(data_0), .b(data_1), .out(divider_2_out), .rem(divider_2_rem));  // open: upper
  // NOT_Gate not_1 is placed but not wired
  // NOT_Gate not_2 is placed but not wired
  // NOT_Gate not_3 is placed but not wired
  FPDivider fpdivider_1 (.a(data_0), .b(data_1), .out(fpdivider_1_out));
  Shifter #(.width(32)) shifter_1 (.in(data_0), .out(shifter_1_out));  // open: dist
  Shifter #(.shift("lr"), .width(32)) shifter_2 (.in(data_0), .out(shifter_2_out));  // open: dist
  Shifter #(.shift("ar"), .width(32)) shifter_3 (.in(data_0), .out(shifter_3_out));  // open: dist
  // OR_Gate or_1 is placed but not wired
  // NOR_Gate nor_1 is placed but not wired
  // XOR_Gate xor_1 is placed but not wired
  // AND_Gate and_1 is placed but not wired
  // NAND_Gate nand_1 is placed but not wired
  // XOR_Gate xor_2 is placed but not wired
  Comparator #(.width(32)) comparator_5 (.a(data_0), .b(data_1));  // open: gt, eq, lt
  Comparator #(.width(32)) comparator_6 (.a(data_0), .b(data_1));  // open: gt, eq, lt
  // FPComparator fpcomparator_1: pin names not known; wires that end beside it: data_0, data_1
  Multiplexer #(.select(5), .width(32)) multiplexer_1 (
    .in0(adder_1_out), .in1(adder_2_out), .in2(fpadder_1_out), .in3(subtractor_1_out),
    .in4(subtractor_2_out), .in5(fpsubtractor_1_out), .in6(multiplier_1_out), .in7(multiplier_2_out),
    .in8(fpmultiplier_1_out), .in9(divider_1_out), .in10(divider_2_out), .in11(fpdivider_1_out),
    .in12(shifter_1_out), .in13(shifter_2_out), .in14(shifter_3_out), .out(out_4), .sel(select_oper));  // open: in15, in16, in17, in18, in19, in20, in21, in22, in23, in24, in25, in26, in27, in28, in29, in30, in31
  Multiplexer #(.select(5)) multiplexer_2 (
    .in0(adder_1_cout), .in1(adder_2_cout), .in2(undriven_4), .in3(subtractor_1_bout),
    .in4(subtractor_2_bout), .in5(undriven_3), .in6(comparator_4_lt), .in7(comparator_3_lt),
    .in8(undriven_2), .in9(comparator_2_eq), .in10(comparator_1_eq), .in11(undriven), .in12(1'b0),
    .in13(1'b0), .in14(1'b0), .out(out_5), .sel(select_oper));  // open: in15, in16, in17, in18, in19, in20, in21, in22, in23, in24, in25, in26, in27, in28, in29, in30, in31
endmodule

module register_file (
  input  clock,
  input  WE,
  input  reset,
  input  [4:0] R1,
  input  [4:0] R2,
  input  [31:0] WD,
  output [31:0] R1D,
  output [31:0] R2D
);

  wire DMX0, DMX1, DMX2, DMX3, DMX4, DMX5, DMX6, DMX7, DMX8, DMX9, DMX10, DMX11, DMX12, DMX13, DMX14, DMX15,
       DMX16, DMX17, DMX18, DMX19, DMX20, DMX21, DMX22, DMX23, DMX24, DMX25, DMX26, DMX27, DMX28, DMX29,
       DMX30, DMX31;
  wire [31:0] register_1_q, register_2_q, register_3_q, register_4_q, register_5_q, register_6_q,
       register_7_q, register_8_q, register_9_q, register_10_q, register_11_q, register_12_q, register_13_q,
       register_14_q, register_15_q, register_16_q, register_17_q, register_18_q, register_19_q,
       register_20_q, register_21_q, register_22_q, register_23_q, register_24_q, register_25_q,
       register_26_q, register_27_q, register_28_q, register_29_q, register_30_q, register_31_q, WD3;

  Register #(.width(32)) register_1 (.D(WD), .en(DMX1), .clk(clock), .Q(register_1_q), .clr(reset));
  Register #(.width(32)) register_2 (.D(WD), .en(DMX2), .clk(clock), .Q(register_2_q), .clr(reset));
  Register #(.width(32)) register_3 (.D(WD), .en(DMX3), .clk(clock), .Q(register_3_q), .clr(reset));
  Register #(.width(32)) register_4 (.D(WD), .en(DMX4), .clk(clock), .Q(register_4_q), .clr(reset));
  Register #(.width(32)) register_5 (.D(WD), .en(DMX5), .clk(clock), .Q(register_5_q), .clr(reset));
  Register #(.width(32)) register_6 (.D(WD), .en(DMX6), .clk(clock), .Q(register_6_q), .clr(reset));
  Register #(.width(32)) register_7 (.D(WD), .en(DMX7), .clk(clock), .Q(register_7_q), .clr(reset));
  Demultiplexer #(.select(5)) demultiplexer_1 (
    .out0(DMX0), .out1(DMX1), .out2(DMX2), .out3(DMX3), .out4(DMX4), .out5(DMX5), .out6(DMX6), .out7(DMX7),
    .out8(DMX8), .out9(DMX9), .out10(DMX10), .out11(DMX11), .out12(DMX12), .out13(DMX13), .out14(DMX14),
    .out15(DMX15), .out16(DMX16), .out17(DMX17), .out18(DMX18), .out19(DMX19), .out20(DMX20), .out21(DMX21),
    .out22(DMX22), .out23(DMX23), .out24(DMX24), .out25(DMX25), .out26(DMX26), .out27(DMX27), .out28(DMX28),
    .out29(DMX29), .out30(DMX30), .out31(DMX31), .in(WE), .sel(R1));
  Register #(.width(32)) register_8 (.D(WD3), .en(DMX8), .clk(clock), .Q(register_8_q), .clr(reset));
  Register #(.width(32)) register_9 (.D(WD3), .en(DMX9), .clk(clock), .Q(register_9_q), .clr(reset));
  Register #(.width(32)) register_10 (.D(WD3), .en(DMX10), .clk(clock), .Q(register_10_q), .clr(reset));
  Register #(.width(32)) register_11 (.D(WD3), .en(DMX11), .clk(clock), .Q(register_11_q), .clr(reset));
  Register #(.width(32)) register_12 (.D(WD3), .en(DMX12), .clk(clock), .Q(register_12_q), .clr(reset));
  Register #(.width(32)) register_13 (.D(WD3), .en(DMX13), .clk(clock), .Q(register_13_q), .clr(reset));
  Register #(.width(32)) register_14 (.D(WD3), .en(DMX14), .clk(clock), .Q(register_14_q), .clr(reset));
  Register #(.width(32)) register_15 (.D(WD3), .en(DMX15), .clk(clock), .Q(register_15_q), .clr(reset));
  Register #(.width(32)) register_16 (.D(WD3), .en(DMX16), .clk(clock), .Q(register_16_q), .clr(reset));
  Register #(.width(32)) register_17 (.D(WD3), .en(DMX17), .clk(clock), .Q(register_17_q), .clr(reset));
  Register #(.width(32)) register_18 (.D(WD3), .en(DMX18), .clk(clock), .Q(register_18_q), .clr(reset));
  Register #(.width(32)) register_19 (.D(WD3), .en(DMX19), .clk(clock), .Q(register_19_q), .clr(reset));
  Register #(.width(32)) register_20 (.D(WD3), .en(DMX20), .clk(clock), .Q(register_20_q), .clr(reset));
  Register #(.width(32)) register_21 (.D(WD3), .en(DMX21), .clk(clock), .Q(register_21_q), .clr(reset));
  Register #(.width(32)) register_22 (.D(WD3), .en(DMX22), .clk(clock), .Q(register_22_q), .clr(reset));
  Register #(.width(32)) register_23 (.D(WD3), .en(DMX23), .clk(clock), .Q(register_23_q), .clr(reset));
  Register #(.width(32)) register_24 (.D(WD3), .en(DMX24), .clk(clock), .Q(register_24_q), .clr(reset));
  Register #(.width(32)) register_25 (.D(WD3), .en(DMX25), .clk(clock), .Q(register_25_q), .clr(reset));
  Register #(.width(32)) register_26 (.D(WD3), .en(DMX26), .clk(clock), .Q(register_26_q), .clr(reset));
  Register #(.width(32)) register_27 (.D(WD3), .en(DMX27), .clk(clock), .Q(register_27_q), .clr(reset));
  Register #(.width(32)) register_28 (.D(WD3), .en(DMX28), .clk(clock), .Q(register_28_q), .clr(reset));
  Register #(.width(32)) register_29 (.D(WD3), .en(DMX29), .clk(clock), .Q(register_29_q), .clr(reset));
  Register #(.width(32)) register_30 (.D(WD3), .en(DMX30), .clk(clock), .Q(register_30_q), .clr(reset));
  Register #(.width(32)) register_31 (.D(WD3), .en(DMX31), .clk(clock), .Q(register_31_q), .clr(reset));
  Multiplexer #(.select(5), .width(32)) multiplexer_1 (
    .in0({32{1'b0}}), .in1(register_1_q), .in2(register_2_q), .in3(register_3_q), .in4(register_4_q),
    .in5(register_5_q), .in6(register_6_q), .in7(register_7_q), .in8(register_8_q), .in9(register_9_q),
    .in10(register_10_q), .in11(register_11_q), .in12(register_12_q), .in13(register_13_q),
    .in14(register_14_q), .in15(register_15_q), .in16(register_16_q), .in17(register_17_q),
    .in18(register_18_q), .in19(register_19_q), .in20(register_20_q), .in21(register_21_q),
    .in22(register_22_q), .in23(register_23_q), .in24(register_24_q), .in25(register_25_q),
    .in26(register_26_q), .in27(register_27_q), .in28(register_28_q), .in29(register_29_q),
    .in30(register_30_q), .in31(register_31_q), .out(R1D), .sel(R1));
  Multiplexer #(.select(5), .width(32)) multiplexer_2 (
    .in0({32{1'b0}}), .in1(register_1_q), .in2(register_2_q), .in3(register_3_q), .in4(register_4_q),
    .in5(register_5_q), .in6(register_6_q), .in7(register_7_q), .in8(register_8_q), .in9(register_9_q),
    .in10(register_10_q), .in11(register_11_q), .in12(register_12_q), .in13(register_13_q),
    .in14(register_14_q), .in15(register_15_q), .in16(register_16_q), .in17(register_17_q),
    .in18(register_18_q), .in19(register_19_q), .in20(register_20_q), .in21(register_21_q),
    .in22(register_22_q), .in23(register_23_q), .in24(register_24_q), .in25(register_25_q),
    .in26(register_26_q), .in27(register_27_q), .in28(register_28_q), .in29(register_29_q),
    .in30(register_30_q), .in31(register_31_q), .out(R2D), .sel(R2));

  // Other names for the same wires on the sheet: RS[4:0] = R1
endmodule

module control_unit (
  input  [5:0] opcode,
  input  [5:0] funct,
  output Jump,
  output MemtoReg,
  output MemWrite,
  output Branch,
  output [2:0] ALUControl,
  output ALUSrc,
  output RegDst,
  output RegWrite
);

  wire [1:0] control_unit_main_decoder_1_aluop;

  control_unit_main_decoder control_unit_main_decoder_1 (
    .opcode(opcode), .Jump(Jump), .RegWrite(RegWrite), .RegDst(RegDst), .ALUSrc(ALUSrc), .Branch(Branch),
    .MemWrite(MemWrite), .MemtoReg(MemtoReg), .ALUOp(control_unit_main_decoder_1_aluop));
  control_unit_alu_decoder control_unit_alu_decoder_1 (
    .ALUOp(control_unit_main_decoder_1_aluop), .funct(funct), .ALUControl(ALUControl));
endmodule

module control_unit_main_decoder (
  input  [5:0] opcode,
  output Jump,
  output RegWrite,
  output RegDst,
  output ALUSrc,
  output Branch,
  output MemWrite,
  output MemtoReg,
  output [1:0] ALUOp
);

  wire comparator_1_eq, comparator_2_eq, comparator_3_eq, comparator_4_eq, comparator_5_eq, comparator_6_eq,
       comparator_7_eq;

  Comparator #(.width(6)) comparator_1 (.a({6{1'b0}}), .b(opcode), .eq(comparator_1_eq));  // open: gt, lt
  Comparator #(.width(6)) comparator_2 (.a(6'b100011), .b(opcode), .eq(comparator_2_eq));  // open: gt, lt
  Comparator #(.width(6)) comparator_3 (.a(6'b101011), .b(opcode), .eq(comparator_3_eq));  // open: gt, lt
  Comparator #(.width(6)) comparator_4 (.a(6'b000100), .b(opcode), .eq(comparator_4_eq));  // open: gt, lt
  Comparator #(.width(6)) comparator_5 (.a(6'b001000), .b(opcode), .eq(comparator_5_eq));  // open: gt, lt
  Comparator #(.width(6)) comparator_6 (.a(6'b001001), .b(opcode), .eq(comparator_6_eq));  // open: gt, lt
  Comparator #(.width(6)) comparator_7 (.a(6'b000010), .b(opcode), .eq(comparator_7_eq));  // open: gt, lt
  buf or_1 (Jump, comparator_7_eq);  // OR_Gate
  or or_2 (RegWrite, comparator_1_eq, comparator_2_eq, comparator_5_eq, comparator_6_eq);
  buf or_3 (RegDst, comparator_1_eq);  // OR_Gate
  or or_4 (ALUSrc, comparator_2_eq, comparator_3_eq, comparator_5_eq, comparator_6_eq);
  buf or_5 (Branch, comparator_4_eq);  // OR_Gate
  buf or_6 (MemWrite, comparator_3_eq);  // OR_Gate
  buf or_7 (MemtoReg, comparator_2_eq);  // OR_Gate
  buf ALUOp1 (ALUOp[1], comparator_1_eq);  // OR_Gate
  or ALUOp0 (ALUOp[0], comparator_4_eq, comparator_6_eq);

  // Notes on the sheet:
  //   lw
  //   sw
  //   beq
  //   addi
  //   subi
  //   j
  //   R-type
endmodule

module control_unit_alu_decoder (
  input  [1:0] ALUOp,
  input  [5:0] funct,
  output [2:0] ALUControl
);

  wire comparator_1_eq, comparator_2_eq, comparator_3_eq, comparator_4_eq, comparator_5_eq, comparator_6_eq,
       comparator_7_eq, comparator_8_eq, comparator_9_eq, or_1_out;
  wire [2:0] controlled_buffer_1_out, controlled_buffer_2_out;

  Comparator #(.mode("unsigned"), .width(2)) comparator_1 (.a(2'b00), .b(ALUOp), .eq(comparator_1_eq));  // open: gt, lt
  Comparator #(.mode("unsigned"), .width(2)) comparator_2 (.a(ALUOp), .b(2'b01), .eq(comparator_2_eq));  // open: gt, lt
  Comparator #(.mode("unsigned"), .width(2)) comparator_3 (.a(ALUOp), .b(2'b10), .eq(comparator_3_eq));  // open: gt, lt
  Comparator #(.mode("unsigned"), .width(2)) comparator_4 (.a(ALUOp), .b(2'b11), .eq(comparator_4_eq));  // open: gt, lt
  Comparator #(.mode("unsigned"), .width(6)) comparator_5 (
    .a(6'b100000), .b(funct), .eq(comparator_5_eq));  // open: gt, lt
  Comparator #(.mode("unsigned"), .width(6)) comparator_6 (
    .a(6'b100010), .b(funct), .eq(comparator_6_eq));  // open: gt, lt
  Comparator #(.mode("unsigned"), .width(6)) comparator_7 (
    .a(6'b100100), .b(funct), .eq(comparator_7_eq));  // open: gt, lt
  Comparator #(.mode("unsigned"), .width(6)) comparator_8 (
    .a(6'b100101), .b(funct), .eq(comparator_8_eq));  // open: gt, lt
  Comparator #(.mode("unsigned"), .width(6)) comparator_9 (
    .a(6'b101010), .b(funct), .eq(comparator_9_eq));  // open: gt, lt
  assign controlled_buffer_1_out = comparator_1_eq ? 3'b010 : 3'bz;  // Controlled_Buffer controlled_buffer_1
  assign controlled_buffer_2_out = comparator_5_eq ? 3'b010 : 3'bz;  // Controlled_Buffer controlled_buffer_2
  assign controlled_buffer_2_out = comparator_6_eq ? 3'b110 : 3'bz;  // Controlled_Buffer controlled_buffer_3
  assign controlled_buffer_2_out = comparator_7_eq ? 3'b000 : 3'bz;  // Controlled_Buffer controlled_buffer_4
  assign controlled_buffer_2_out = comparator_8_eq ? 3'b001 : 3'bz;  // Controlled_Buffer controlled_buffer_5
  assign controlled_buffer_2_out = comparator_9_eq ? 3'b111 : 3'bz;  // Controlled_Buffer controlled_buffer_6
  or or_1 (or_1_out, comparator_2_eq, comparator_4_eq);
  assign controlled_buffer_1_out = or_1_out ? 3'b110 : 3'bz;  // Controlled_Buffer controlled_buffer_7
  Multiplexer #(.width(3)) multiplexer_1 (
    .in0(controlled_buffer_1_out), .in1(controlled_buffer_2_out), .out(ALUControl), .sel(comparator_3_eq));

  // Notes on the sheet:
  //   00
  //   01
  //   10
  //   11
  //   add
  //   sub
  //   and
  //   or
  //   slt
endmodule

module multiplexor6bit (
  input  [5:0] selector,
  input  [31:0] in_2,
  input  [31:0] in_3,
  input  [31:0] in_4,
  input  [31:0] in_5,
  input  [31:0] in_6,
  input  [31:0] in_7,
  input  [31:0] in_8,
  input  [31:0] in_9,
  input  [31:0] in_10,
  input  [31:0] in_11,
  input  [31:0] in_12,
  input  [31:0] in_13,
  input  [31:0] in_14,
  input  [31:0] in_15,
  input  [31:0] in_16,
  input  [31:0] in_17,
  input  [31:0] in_18,
  input  [31:0] in_19,
  input  [31:0] in_20,
  input  [31:0] in_21,
  input  [31:0] in_22,
  input  [31:0] in_23,
  input  [31:0] in_24,
  input  [31:0] in_25,
  input  [31:0] in_26,
  input  [31:0] in_27,
  input  [31:0] in_28,
  input  [31:0] in_29,
  input  [31:0] in_30,
  input  [31:0] in_31,
  input  [31:0] in_32,
  input  [31:0] in_33,
  input  [31:0] in_34,
  input  [31:0] in_35,
  input  [31:0] in_36,
  input  [31:0] in_37,
  input  [31:0] in_38,
  input  [31:0] in_39,
  input  [31:0] in_40,
  input  [31:0] in_41,
  input  [31:0] in_42,
  input  [31:0] in_43,
  input  [31:0] in_44,
  input  [31:0] in_45,
  input  [31:0] in_46,
  input  [31:0] in_47,
  input  [31:0] in_48,
  input  [31:0] in_49,
  input  [31:0] in_50,
  input  [31:0] in_51,
  input  [31:0] in_52,
  input  [31:0] in_53,
  input  [31:0] in_54,
  input  [31:0] in_55,
  input  [31:0] in_56,
  input  [31:0] in_57,
  input  [31:0] in_58,
  input  [31:0] in_59,
  input  [31:0] in_60,
  input  [31:0] in_61,
  input  [31:0] in_62,
  input  [31:0] in_63,
  input  [31:0] in_64,
  input  [31:0] in_65,
  output [31:0] out_66
);

  wire not_1_out;
  wire [31:0] multiplexer_1_out, multiplexer_2_out;

  Multiplexer #(.select(5), .width(32)) multiplexer_1 (
    .in0(in_2), .in1(in_3), .in2(in_4), .in3(in_5), .in4(in_6), .in5(in_7), .in6(in_8), .in7(in_9),
    .in8(in_10), .in9(in_11), .in10(in_12), .in11(in_13), .in12(in_14), .in13(in_15), .in14(in_16),
    .in15(in_17), .in16(in_18), .in17(in_19), .in18(in_20), .in19(in_21), .in20(in_22), .in21(in_23),
    .in22(in_24), .in23(in_25), .in24(in_26), .in25(in_27), .in26(in_28), .in27(in_29), .in28(in_30),
    .in29(in_31), .in30(in_32), .in31(in_33), .out(multiplexer_1_out), .sel(selector[4:0]));
  Multiplexer #(.select(5), .width(32)) multiplexer_2 (
    .in0(in_34), .in1(in_35), .in2(in_36), .in3(in_37), .in4(in_38), .in5(in_39), .in6(in_40), .in7(in_41),
    .in8(in_42), .in9(in_43), .in10(in_44), .in11(in_45), .in12(in_46), .in13(in_47), .in14(in_48),
    .in15(in_49), .in16(in_50), .in17(in_51), .in18(in_52), .in19(in_53), .in20(in_54), .in21(in_55),
    .in22(in_56), .in23(in_57), .in24(in_58), .in25(in_59), .in26(in_60), .in27(in_61), .in28(in_62),
    .in29(in_63), .in30(in_64), .in31(in_65), .out(multiplexer_2_out), .sel(selector[4:0]));
  not not_1 (not_1_out, selector[5]);
  gate32bit gate32bit_1 (.enable(selector[5]), .data(multiplexer_2_out), .out_3(out_66));
  gate32bit gate32bit_2 (.enable(not_1_out), .data(multiplexer_1_out), .out_3(out_66));
endmodule

module gate32bit (
  input  enable,
  input  [31:0] data,
  output [31:0] out_3
);

  wire [31:0] and_1_out, bit_extender_1_out;

  assign bit_extender_1_out = {{31{enable}}, enable};  // Bit_Extender bit_extender_1
  assign and_1_out = bit_extender_1_out & data;  // AND_Gate and_1, 32 bits wide
  assign out_3 = enable ? and_1_out : 32'bz;  // Controlled_Buffer controlled_buffer_1
endmodule
